# Fritzing sketch pi_rgb_led (saved by Fritzing 0.9.3b)
circuit board: 8.46667cm x 5.64444cm
breadboards: 1

parts:
  12v_In = Power Jack [package=power_jack_pth]
  Q3-G = Basic FET N-Channel [package="DPak [SMD]"]
  R3 = Resistor [tolerance=±5% resistance=10k package="0402 [SMD]"]
  Q2-R = Basic FET N-Channel [package="DPak [SMD]"]
  R2 = Resistor [tolerance=±5% resistance=10k package="0402 [SMD]"]
  Q1-B = Basic FET N-Channel [package="DPak [SMD]"]
  R1 = Resistor [tolerance=±5% resistance=10k package="0402 [SMD]"]
  LED_Out = female pin header, 4 pins [form="♀ (female)"]
  Common_Anode_RGB_LED_Strip = female pin header, 4 pins [form="♀ (female)"]
  Raspberry_Pi_1 = Raspberry Pi 3 [part_number=RPI-3-V1.2]

nets (from the breadboard view):
  GND: 12v_In.GND, 12v_In.GNDBREAK, Q3-G.source, R3.Pin_0, Q2-R.source, R2.Pin_0, Q1-B.source, R1.Pin_0, Raspberry_Pi_1.GND
  N1: 12v_In.PWR, LED_Out.pin1, Common_Anode_RGB_LED_Strip.pin1
  N2: Q3-G.Gate, Raspberry_Pi_1.GPIO13
  N3: Q3-G.drain, R3.Pin_1, LED_Out.pin2, Common_Anode_RGB_LED_Strip.pin2
  N4: Q2-R.Gate, Raspberry_Pi_1.GPIO6
  N5: Q2-R.drain, R2.Pin_1, LED_Out.pin3, Common_Anode_RGB_LED_Strip.pin3
  N6: Q1-B.Gate, Raspberry_Pi_1.GPIO5
  N7: Q1-B.drain, R1.Pin_1, LED_Out.pin4, Common_Anode_RGB_LED_Strip.pin4

notes:
  12v Rail
  3.3v Rail
